// Logisim project SAP-3 Logisim.circ as structural Verilog: 3 circuits, main circuit main
module main (
);

  wire [7:0] n8_bit_alu_1_output, undriven, undriven_2;

  _8_Bit_ALU u_8_bit_alu_1 (
    .Output(n8_bit_alu_1_output), .Input_A(undriven), .Input_B(undriven_2));  // open: AD__Add, SU__Subtract, NA__NAND, NO__NOR, XO__XOR
  // Probe on n8_bit_alu_1_output
endmodule

module Full_Adder_Module (
  input  A,
  input  B,
  input  Carry_In,
  output Sum,
  output Carry_Out
);

  wire and_1_out, and_2_out, xor_1_out;

  xor xor_1 (xor_1_out, A, B);
  and and_1 (and_1_out, A, B);
  xor xor_2 (Sum, xor_1_out, Carry_In);
  and and_2 (and_2_out, xor_1_out, Carry_In);
  or or_1 (Carry_Out, and_2_out, and_1_out);
endmodule

// ALU
module _8_Bit_ALU (
  input  [7:0] Input_A,
  input  AD__Add,
  input  SU__Subtract,
  input  NA__NAND,
  input  NO__NOR,
  input  XO__XOR,
  input  [7:0] Input_B,
  output [7:0] Output
);

  wire controlled_buffer_1_out, controlled_buffer_2_out, controlled_buffer_3_out, controlled_buffer_4_out,
       controlled_buffer_5_out, controlled_buffer_6_out, controlled_buffer_7_out, controlled_buffer_8_out,
       full_adder_module_1_carry_out, full_adder_module_1_sum, full_adder_module_2_carry_out,
       full_adder_module_2_sum, full_adder_module_3_carry_out, full_adder_module_3_sum,
       full_adder_module_4_carry_out, full_adder_module_4_sum, full_adder_module_5_carry_out,
       full_adder_module_5_sum, full_adder_module_6_carry_out, full_adder_module_6_sum,
       full_adder_module_7_carry_out, full_adder_module_7_sum, full_adder_module_8_sum, nand_1_out,
       nand_2_out, nand_3_out, nand_4_out, nand_5_out, nand_6_out, nand_7_out, nand_8_out, nor_1_out,
       nor_2_out, nor_3_out, nor_4_out, nor_5_out, nor_6_out, nor_7_out, nor_8_out, or_1_out, or_2_out,
       xor_1_out, xor_2_out, xor_3_out, xor_4_out, xor_5_out, xor_6_out, xor_7_out, xor_8_out, xor_9_out,
       xor_10_out, xor_11_out, xor_12_out, xor_13_out, xor_14_out, xor_15_out, xor_16_out;

  or or_1 (or_1_out, AD__Add, SU__Subtract, NA__NAND, NO__NOR, XO__XOR);
  or or_2 (or_2_out, AD__Add, SU__Subtract);
  xor xor_1 (xor_1_out, SU__Subtract, Input_B[6]);
  xor xor_2 (xor_2_out, SU__Subtract, Input_B[7]);
  xor xor_3 (xor_3_out, SU__Subtract, Input_B[5]);
  xor xor_4 (xor_4_out, SU__Subtract, Input_B[4]);
  xor xor_5 (xor_5_out, SU__Subtract, Input_B[3]);
  xor xor_6 (xor_6_out, SU__Subtract, Input_B[2]);
  xor xor_7 (xor_7_out, SU__Subtract, Input_B[0]);
  xor xor_8 (xor_8_out, SU__Subtract, Input_B[1]);
  Full_Adder_Module full_adder_module_1 (
    .A(Input_A[0]), .B(xor_7_out), .Carry_In(SU__Subtract), .Sum(full_adder_module_1_sum),
    .Carry_Out(full_adder_module_1_carry_out));
  nand nand_1 (nand_1_out, Input_A[7], xor_2_out);
  nand nand_2 (nand_2_out, Input_A[6], xor_1_out);
  nand nand_3 (nand_3_out, Input_A[5], xor_3_out);
  nand nand_4 (nand_4_out, Input_A[4], xor_4_out);
  nand nand_5 (nand_5_out, Input_A[3], xor_5_out);
  nand nand_6 (nand_6_out, Input_A[2], xor_6_out);
  nand nand_7 (nand_7_out, Input_A[1], xor_8_out);
  nand nand_8 (nand_8_out, Input_A[0], xor_7_out);
  nor nor_1 (nor_1_out, Input_A[7], xor_2_out);
  nor nor_2 (nor_2_out, Input_A[6], xor_1_out);
  nor nor_3 (nor_3_out, Input_A[5], xor_3_out);
  nor nor_4 (nor_4_out, Input_A[4], xor_4_out);
  nor nor_5 (nor_5_out, Input_A[3], xor_5_out);
  nor nor_6 (nor_6_out, Input_A[2], xor_6_out);
  nor nor_7 (nor_7_out, Input_A[1], xor_8_out);
  nor nor_8 (nor_8_out, Input_A[0], xor_7_out);
  xor xor_9 (xor_9_out, Input_A[7], xor_2_out);
  xor xor_10 (xor_10_out, Input_A[6], xor_1_out);
  xor xor_11 (xor_11_out, Input_A[5], xor_3_out);
  xor xor_12 (xor_12_out, Input_A[4], xor_4_out);
  xor xor_13 (xor_13_out, Input_A[3], xor_5_out);
  xor xor_14 (xor_14_out, Input_A[2], xor_6_out);
  xor xor_15 (xor_15_out, Input_A[1], xor_8_out);
  xor xor_16 (xor_16_out, Input_A[0], xor_7_out);
  Full_Adder_Module full_adder_module_2 (
    .A(Input_A[2]), .B(xor_6_out), .Carry_In(full_adder_module_3_carry_out), .Sum(full_adder_module_2_sum),
    .Carry_Out(full_adder_module_2_carry_out));
  Full_Adder_Module full_adder_module_3 (
    .A(Input_A[1]), .B(xor_8_out), .Carry_In(full_adder_module_1_carry_out), .Sum(full_adder_module_3_sum),
    .Carry_Out(full_adder_module_3_carry_out));
  assign controlled_buffer_1_out = NA__NAND ? nand_1_out : 1'bz;  // Controlled_Buffer controlled_buffer_1
  assign controlled_buffer_2_out = NA__NAND ? nand_2_out : 1'bz;  // Controlled_Buffer controlled_buffer_2
  assign controlled_buffer_3_out = NA__NAND ? nand_3_out : 1'bz;  // Controlled_Buffer controlled_buffer_3
  assign controlled_buffer_4_out = NA__NAND ? nand_4_out : 1'bz;  // Controlled_Buffer controlled_buffer_4
  assign controlled_buffer_5_out = NA__NAND ? nand_5_out : 1'bz;  // Controlled_Buffer controlled_buffer_5
  assign controlled_buffer_6_out = NA__NAND ? nand_6_out : 1'bz;  // Controlled_Buffer controlled_buffer_6
  assign controlled_buffer_7_out = NA__NAND ? nand_7_out : 1'bz;  // Controlled_Buffer controlled_buffer_7
  assign controlled_buffer_8_out = NA__NAND ? nand_8_out : 1'bz;  // Controlled_Buffer controlled_buffer_8
  assign controlled_buffer_1_out = NO__NOR ? nor_1_out : 1'bz;  // Controlled_Buffer controlled_buffer_9
  assign controlled_buffer_2_out = NO__NOR ? nor_2_out : 1'bz;  // Controlled_Buffer controlled_buffer_10
  assign controlled_buffer_3_out = NO__NOR ? nor_3_out : 1'bz;  // Controlled_Buffer controlled_buffer_11
  assign controlled_buffer_4_out = NO__NOR ? nor_4_out : 1'bz;  // Controlled_Buffer controlled_buffer_12
  assign controlled_buffer_5_out = NO__NOR ? nor_5_out : 1'bz;  // Controlled_Buffer controlled_buffer_13
  assign controlled_buffer_6_out = NO__NOR ? nor_6_out : 1'bz;  // Controlled_Buffer controlled_buffer_14
  assign controlled_buffer_7_out = NO__NOR ? nor_7_out : 1'bz;  // Controlled_Buffer controlled_buffer_15
  assign controlled_buffer_8_out = NO__NOR ? nor_8_out : 1'bz;  // Controlled_Buffer controlled_buffer_16
  assign controlled_buffer_1_out = XO__XOR ? xor_9_out : 1'bz;  // Controlled_Buffer controlled_buffer_17
  assign controlled_buffer_2_out = XO__XOR ? xor_10_out : 1'bz;  // Controlled_Buffer controlled_buffer_18
  assign controlled_buffer_3_out = XO__XOR ? xor_11_out : 1'bz;  // Controlled_Buffer controlled_buffer_19
  assign controlled_buffer_4_out = XO__XOR ? xor_12_out : 1'bz;  // Controlled_Buffer controlled_buffer_20
  assign controlled_buffer_5_out = XO__XOR ? xor_13_out : 1'bz;  // Controlled_Buffer controlled_buffer_21
  assign controlled_buffer_6_out = XO__XOR ? xor_14_out : 1'bz;  // Controlled_Buffer controlled_buffer_22
  assign controlled_buffer_7_out = XO__XOR ? xor_15_out : 1'bz;  // Controlled_Buffer controlled_buffer_23
  assign controlled_buffer_8_out = XO__XOR ? xor_16_out : 1'bz;  // Controlled_Buffer controlled_buffer_24
  Full_Adder_Module full_adder_module_4 (
    .A(Input_A[3]), .B(xor_5_out), .Carry_In(full_adder_module_2_carry_out), .Sum(full_adder_module_4_sum),
    .Carry_Out(full_adder_module_4_carry_out));
  Full_Adder_Module full_adder_module_5 (
    .A(Input_A[5]), .B(xor_3_out), .Carry_In(full_adder_module_6_carry_out), .Sum(full_adder_module_5_sum),
    .Carry_Out(full_adder_module_5_carry_out));
  Full_Adder_Module full_adder_module_6 (
    .A(Input_A[4]), .B(xor_4_out), .Carry_In(full_adder_module_4_carry_out), .Sum(full_adder_module_6_sum),
    .Carry_Out(full_adder_module_6_carry_out));
  Full_Adder_Module full_adder_module_7 (
    .A(Input_A[6]), .B(xor_1_out), .Carry_In(full_adder_module_5_carry_out), .Sum(full_adder_module_7_sum),
    .Carry_Out(full_adder_module_7_carry_out));
  Full_Adder_Module full_adder_module_8 (
    .A(Input_A[7]), .B(xor_2_out), .Carry_In(full_adder_module_7_carry_out), .Sum(full_adder_module_8_sum));  // open: Carry_Out
  assign controlled_buffer_1_out = or_2_out ? full_adder_module_8_sum : 1'bz;  // Controlled_Buffer controlled_buffer_25
  assign controlled_buffer_2_out = or_2_out ? full_adder_module_7_sum : 1'bz;  // Controlled_Buffer controlled_buffer_26
  assign controlled_buffer_3_out = or_2_out ? full_adder_module_5_sum : 1'bz;  // Controlled_Buffer controlled_buffer_27
  assign controlled_buffer_4_out = or_2_out ? full_adder_module_6_sum : 1'bz;  // Controlled_Buffer controlled_buffer_28
  assign controlled_buffer_5_out = or_2_out ? full_adder_module_4_sum : 1'bz;  // Controlled_Buffer controlled_buffer_29
  assign controlled_buffer_6_out = or_2_out ? full_adder_module_2_sum : 1'bz;  // Controlled_Buffer controlled_buffer_30
  assign controlled_buffer_7_out = or_2_out ? full_adder_module_3_sum : 1'bz;  // Controlled_Buffer controlled_buffer_31
  assign controlled_buffer_8_out = or_2_out ? full_adder_module_1_sum : 1'bz;  // Controlled_Buffer controlled_buffer_32
  assign Output[0] = or_1_out ? controlled_buffer_1_out : 1'bz;  // Controlled_Buffer controlled_buffer_33
  assign Output[1] = or_1_out ? controlled_buffer_2_out : 1'bz;  // Controlled_Buffer controlled_buffer_34
  assign Output[2] = or_1_out ? controlled_buffer_3_out : 1'bz;  // Controlled_Buffer controlled_buffer_35
  assign Output[3] = or_1_out ? controlled_buffer_4_out : 1'bz;  // Controlled_Buffer controlled_buffer_36
  assign Output[4] = or_1_out ? controlled_buffer_5_out : 1'bz;  // Controlled_Buffer controlled_buffer_37
  assign Output[5] = or_1_out ? controlled_buffer_6_out : 1'bz;  // Controlled_Buffer controlled_buffer_38
  assign Output[6] = or_1_out ? controlled_buffer_7_out : 1'bz;  // Controlled_Buffer controlled_buffer_39
  assign Output[7] = or_1_out ? controlled_buffer_8_out : 1'bz;  // Controlled_Buffer controlled_buffer_40

  // Notes on the sheet:
  //   Control Signals
  //   Bus Output
endmodule
